# Fritzing sketch SpO2 (saved by Fritzing 0.9.10b)
breadboards: 1

parts:
  Mod1 = Amica NodeMCU DEVKIT 1.0
  M1 = GY-MAX30102
  OLED_I2C1 = OLED 128x64 I2C Monochrome Display

nets:
  VIN: Mod1.pin1, Mod1.pin_10, Mod1.pin_26, M1.VIN, OLED_I2C1.VDD
  GND: Mod1.pin2, Mod1.pin_9, Mod1.pin_25, Mod1.pin_29, M1.GND, OLED_I2C1.GND
  N1: Mod1.pin_13, M1.SDA, OLED_I2C1.SDA
  N2: Mod1.pin_14, M1.SCL, OLED_I2C1.SCK

notes:
  Nguồn

custom parts:
  GY-MAX30102: Oximeter module using the MAX30102 chip. You may wish to read (and check your module) this post on power problems with these modules: https://reedpaper.wordpress.com/2018/08/22/pulse-oximeter-max30100-max30102-how-to-fix-wrong-board/ (may not apply as this is a different module!). As usual, if you want the mounting holes in pcb, you need to drag a hole over the pad in silkscreen to actually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
